# Fritzing sketch optionphone (saved by Fritzing 0.9.3b)
perfboards: 1

parts:
  R1 = Resistor [tolerance=±5% resistance=10k package=THT]  # not connected
  R3 = Resistor [tolerance=±5% resistance=330k package=THT]  # not connected
  R7 = Resistor [tolerance=±5% resistance=330k package=THT]  # not connected
  R9 = Resistor [tolerance=±5% resistance=330k package=THT]
  R10 = Resistor [tolerance=±5% resistance=10k package=THT]
  MCU1 = Raspberry Pi Zero

nets:
  N1: R9.Pin_0, MCU1.pin_1, MCU1.pin_17
  N2: R10.Pin_1, MCU1.pin_26
  N3: MCU1.pin_2, MCU1.pin_4
  N4: MCU1.pin_6, MCU1.pin_9, MCU1.pin_39

notes:
  number counter
  ringer right
  ringer left
  speaker
  handset
